# Fritzing sketch pi-pir (saved by Fritzing 0.9.2b)
breadboards: 1

parts:
  Raspberry_Pi1 = Raspberry Pi 2
  PIR1 = PIR sensor
  R1 = Resistor [tolerance=±5% resistance=10k package=THT]

nets:
  N1: Raspberry_Pi1.GPIO4, PIR1.SIG, R1.Pin_1
  GND: Raspberry_Pi1.GND, PIR1.GND
  5V: Raspberry_Pi1.5V, PIR1.VDD, R1.Pin_0
